// Logisim project elec_clock.circ as structural Verilog: 9 circuits, main circuit main
module main (
);

  // adder4bit adder4bit_1: pin names not known
  // comparator4bit comparator4bit_1: pin names not known
endmodule

module bcd7seg (
  input  D3,
  input  D2,
  input  D1,
  input  D0,
  input  EN,
  input  Point,
  output A,
  output B,
  output C,
  output D,
  output E,
  output F,
  output G,
  output P
);

  wire and_1_out, and_2_out, and_3_out, and_4_out, and_5_out, and_6_out, and_7_out, and_8_out, and_9_out,
       and_10_out, and_11_out, and_12_out, and_13_out, and_14_out, and_15_out, and_16_out, not_1_out,
       not_2_out, not_3_out, or_1_out, or_2_out, or_3_out, or_4_out, or_5_out, or_6_out, or_7_out;

  not not_1 (not_1_out, D2);
  not not_2 (not_2_out, D1);
  not not_3 (not_3_out, D0);
  and and_1 (and_1_out, D2, D0);
  and and_2 (and_2_out, not_1_out, not_3_out);
  and and_3 (and_3_out, D1, D0);
  and and_4 (and_4_out, not_2_out, not_3_out);
  and and_5 (and_5_out, D1, not_3_out);
  and and_6 (and_6_out, D1, not_1_out);
  and and_7 (and_7_out, not_1_out, not_3_out);
  and and_8 (and_8_out, D2, not_2_out, D0);
  and and_9 (and_9_out, D1, not_3_out);
  and and_10 (and_10_out, not_1_out, not_3_out);
  and and_11 (and_11_out, D2, not_3_out);
  and and_12 (and_12_out, D2, not_2_out);
  and and_13 (and_13_out, not_2_out, not_3_out);
  and and_14 (and_14_out, D1, not_3_out);
  and and_15 (and_15_out, D1, not_1_out);
  and and_16 (and_16_out, D2, not_2_out);
  or or_1 (or_1_out, and_1_out, D3, D1, and_2_out);
  or or_2 (or_2_out, and_3_out, not_1_out, and_4_out);
  or or_3 (or_3_out, D2, not_2_out, D0);
  or or_4 (or_4_out, and_5_out, and_6_out, D3, and_7_out, and_8_out);
  or or_5 (or_5_out, and_9_out, and_10_out);
  or or_6 (or_6_out, D3, and_11_out, and_12_out, and_13_out);
  or or_7 (or_7_out, D3, and_14_out, and_15_out, and_16_out);
  _7_Segment_Display u_7_segment_display_1 (
    .g(or_7_out), .f(or_6_out), .a(or_1_out), .b(or_2_out), .e(or_5_out), .d(or_4_out), .c(or_3_out),
    .dp(Point));
  and and_17 (A, or_1_out, EN);
  and and_18 (B, or_2_out, EN);
  and and_19 (C, or_3_out, EN);
  and and_20 (D, or_4_out, EN);
  and and_21 (E, or_5_out, EN);
  and and_22 (F, or_6_out, EN);
  and and_23 (G, or_7_out, EN);

  assign P = Point;
endmodule

module d_latch (
  input  RST,
  input  WE,
  input  D,
  output Q,
  output out_5
);

  wire and_1_out, and_2_out, and_3_out, not_1_out, not_2_out, or_1_out;

  not not_1 (not_1_out, D);
  and and_1 (and_1_out, not_1_out, WE);
  and and_2 (and_2_out, WE, D);
  or or_1 (or_1_out, RST, and_1_out);
  not not_2 (not_2_out, RST);
  and and_3 (and_3_out, not_2_out, and_2_out);
  nor nor_1 (Q, or_1_out, out_5);
  nor nor_2 (out_5, Q, and_3_out);
endmodule

module ms_dff (
  input  EN,
  input  RST,
  input  clk,
  input  D,
  output Q
);

  wire d_latch_1_q, d_latch_2_q;

  d_latch d_latch_1 (.RST(RST), .WE(clk), .D(d_latch_2_q), .Q(d_latch_1_q));  // open: out_5
  d_latch d_latch_2 (.RST(RST), .WE(clk), .D(D), .Q(d_latch_2_q));  // open: out_5
  and and_1 (Q, EN, d_latch_1_q);
endmodule

module mb_dff (
  input  EN,
  input  RST,
  input  clk,
  input  D,
  output Q,
  output out_6
);

  wire and_1_out, G_out, nand_1_out, nand_2_out, nand_3_out, nand_4_out, not_1_out, or_1_out;

  nand nand_1 (nand_1_out, nand_3_out, nand_2_out);
  nand nand_2 (nand_2_out, nand_1_out, clk);
  not not_1 (not_1_out, RST);
  nand G (G_out, nand_2_out, clk, nand_3_out);
  nand nand_3 (nand_3_out, G_out, D);
  or or_1 (or_1_out, RST, nand_2_out);
  and and_1 (and_1_out, not_1_out, G_out);
  nand nand_4 (nand_4_out, or_1_out, out_6);
  nand nand_5 (out_6, nand_4_out, and_1_out);
  and and_2 (Q, EN, nand_4_out);
endmodule

module register4bit (
  input  EN,
  input  clk,
  input  RST,
  input  [3:0] D,
  output [3:0] out_5
);

  mb_dff mb_dff_1 (.EN(EN), .RST(RST), .clk(clk), .D(D[0]), .Q(out_5[0]));  // open: out_6
  mb_dff mb_dff_2 (.EN(EN), .RST(RST), .clk(clk), .D(D[1]), .Q(out_5[1]));  // open: out_6
  mb_dff mb_dff_3 (.EN(EN), .RST(RST), .clk(clk), .D(D[2]), .Q(out_5[2]));  // open: out_6
  mb_dff mb_dff_4 (.EN(EN), .RST(RST), .clk(clk), .D(D[3]), .Q(out_5[3]));  // open: out_6
endmodule

module full_adder (
  input  A,
  input  B,
  input  Cin,
  output S,
  output Cout
);

  wire and_1_out, and_2_out, and_3_out;

  and and_1 (and_1_out, A, B);
  and and_2 (and_2_out, B, Cin);
  and and_3 (and_3_out, A, Cin);
  xor xor_1 (S, A, B, Cin);
  or or_1 (Cout, and_1_out, and_2_out, and_3_out);
endmodule

module adder4bit (
  input  [3:0] A,
  input  [3:0] B,
  input  C,
  output [3:0] S
);

  wire full_adder_1_cout, full_adder_2_cout, full_adder_3_cout, full_adder_4_cout;

  full_adder full_adder_1 (.A(A[0]), .B(B[0]), .Cin(C), .S(S[0]), .Cout(full_adder_1_cout));
  full_adder full_adder_2 (.A(A[1]), .B(B[1]), .Cin(full_adder_1_cout), .S(S[1]), .Cout(full_adder_2_cout));
  full_adder full_adder_3 (.A(A[2]), .B(B[2]), .Cin(full_adder_2_cout), .S(S[2]), .Cout(full_adder_3_cout));
  full_adder full_adder_4 (.A(A[3]), .B(B[3]), .Cin(full_adder_3_cout), .S(S[3]), .Cout(full_adder_4_cout));
  LED led_1 (.in(full_adder_4_cout));
endmodule

module comparator4bit (
  input  [3:0] A,
  input  [3:0] B,
  output Same
);

  wire xnor_1_out, xnor_2_out, xnor_3_out, xnor_4_out;

  xnor xnor_1 (xnor_1_out, A[0], B[0]);
  xnor xnor_2 (xnor_2_out, A[1], B[1]);
  xnor xnor_3 (xnor_3_out, A[2], B[2]);
  xnor xnor_4 (xnor_4_out, A[3], B[3]);
  and and_1 (Same, xnor_1_out, xnor_2_out, xnor_3_out, xnor_4_out);
endmodule
